// Logisim project SAP_1.circ as structural Verilog: 12 circuits, main circuit main
module main (
);

  wire controller_1_clk, controller_1_clr, controller_1_nclk, controller_1_nclr;
  wire [3:0] inputandmar_1_out_4, inputandmar_1_out_5, instructionregister_1_out_7, programcounter_1_out_5,
       ram16x8_1_out_4;
  wire [7:0] accumulatora_1_out_6, bregister_1_out_4, outputregister_1_out_4;
  wire [11:0] controller_1_out_9;

  Register #(.width(4)) register_1 ();  // open: D, en, clk, Q, clr
  ProgramCounter programcounter_1 (
    .Cp(controller_1_out_9[11]), .n_CLK(controller_1_nclk), .n_CLR(controller_1_nclr),
    .Ep(controller_1_out_9[10]), .out_5(programcounter_1_out_5));
  InputAndMAR inputandmar_1 (
    .n_Lm(controller_1_out_9[9]), .CLK(controller_1_clk), .in_1(programcounter_1_out_5),
    .out_4(inputandmar_1_out_4), .out_5(inputandmar_1_out_5));
  RAM16x8 ram16x8_1 (
    .in_1(inputandmar_1_out_4), .in_2(inputandmar_1_out_5), .n_CE(controller_1_out_9[8]),
    .out_4({ram16x8_1_out_4, programcounter_1_out_5}));
  InstructionRegister instructionregister_1 (
    .in_2({ram16x8_1_out_4, programcounter_1_out_5}), .n_Li(controller_1_out_9[7]), .CLK(controller_1_clk),
    .CLR(controller_1_clr), .n_Ei(controller_1_out_9[6]), .out_6(programcounter_1_out_5),
    .out_7(instructionregister_1_out_7));
  Controller controller_1 (
    .in_4(instructionregister_1_out_7), .CLR(controller_1_clr), .nCLR(controller_1_nclr),
    .CLK(controller_1_clk), .nCLK(controller_1_nclk), .out_9(controller_1_out_9));  // open: SingleStep, ManualAuto, StartClear
  LED led_1 (.in(outputregister_1_out_4[7]));
  LED led_2 (.in(outputregister_1_out_4[6]));
  LED led_3 (.in(outputregister_1_out_4[5]));
  AccumulatorA accumulatora_1 (
    .in_1({ram16x8_1_out_4, programcounter_1_out_5}), .CLK(controller_1_clk), .Ea(controller_1_out_9[4]),
    .n_La(controller_1_out_9[5]), .out_5({ram16x8_1_out_4, programcounter_1_out_5}),
    .out_6(accumulatora_1_out_6));
  AdderSubtractor addersubtractor_1 (
    .in_1(accumulatora_1_out_6), .Su(controller_1_out_9[3]), .Eu(controller_1_out_9[2]),
    .out_5({ram16x8_1_out_4, programcounter_1_out_5}));  // open: in_4
  BRegister bregister_1 (
    .in_2({ram16x8_1_out_4, programcounter_1_out_5}), .n_Lb(controller_1_out_9[1]), .CLK(controller_1_clk),
    .out_4(bregister_1_out_4));
  OutputRegister outputregister_1 (
    .in_2({ram16x8_1_out_4, programcounter_1_out_5}), .n_Lo(controller_1_out_9[0]), .CLK(controller_1_clk),
    .out_4(outputregister_1_out_4));
  LED led_4 (.in(outputregister_1_out_4[4]));
  LED led_5 (.in(outputregister_1_out_4[3]));
  LED led_6 (.in(outputregister_1_out_4[2]));
  LED led_7 (.in(outputregister_1_out_4[1]));
  LED led_8 (.in(outputregister_1_out_4[0]));
endmodule

module ProgramCounter (
  input  Cp,
  input  n_CLK,
  input  n_CLR,
  input  Ep,
  output [3:0] out_5
);

  wire [3:0] j_k_ff_1_q;

  J_K_Flip_Flop #(.trigger("falling")) j_k_ff_1 (
    .J(Cp), .K(Cp), .clk(n_CLK), .Q(j_k_ff_1_q[0]), .reset(n_CLR));  // open: Qn, preset
  J_K_Flip_Flop #(.trigger("falling")) j_k_ff_2 (
    .J(Cp), .K(Cp), .clk(j_k_ff_1_q[0]), .Q(j_k_ff_1_q[1]), .reset(n_CLR));  // open: Qn, preset
  J_K_Flip_Flop #(.trigger("falling")) j_k_ff_3 (
    .J(Cp), .K(Cp), .clk(j_k_ff_1_q[1]), .Q(j_k_ff_1_q[2]), .reset(n_CLR));  // open: Qn, preset
  J_K_Flip_Flop #(.trigger("falling")) j_k_ff_4 (
    .J(Cp), .K(Cp), .clk(j_k_ff_1_q[2]), .Q(j_k_ff_1_q[3]), .reset(n_CLR));  // open: Qn, preset
  assign out_5 = Ep ? ~j_k_ff_1_q : 4'bz;  // Controlled_Inverter controlled_inverter_1
endmodule

module InputAndMAR (
  input  [3:0] in_1,
  input  n_Lm,
  input  CLK,
  output [3:0] out_4,
  output [3:0] out_5
);

  Register #(.width(4)) register_1 (.D(in_1), .en(n_Lm), .clk(CLK), .Q(out_4));  // open: clr

  assign out_5 = out_4;
endmodule

module RAM16x8 (
  input  [3:0] in_1,
  input  [3:0] in_2,
  input  n_CE,
  output [7:0] out_4
);

  wire [3:0] ram_1_dout, ram_2_dout, undriven, undriven_2;

  RAM #(.addrWidth(4), .dataWidth(4), .trigger("high")) ram_1 (
    .addr(undriven), .oe(n_CE), .din(in_1), .dout(ram_1_dout));  // open: we
  RAM #(.addrWidth(4), .dataWidth(4), .trigger("high")) ram_2 (
    .addr(in_2), .oe(n_CE), .din(undriven_2), .dout(ram_2_dout));  // open: we
  assign out_4 = n_CE ? {ram_1_dout, ram_2_dout} : 8'bz;  // Controlled_Buffer controlled_buffer_1
endmodule

module InstructionRegister (
  input  n_Li,
  input  [7:0] in_2,
  input  CLK,
  input  CLR,
  input  n_Ei,
  output [3:0] out_6,
  output [3:0] out_7
);

  wire [3:0] register_2_q;

  Register #(.trigger("falling"), .width(4)) register_1 (.D(in_2[7:4]), .en(n_Li), .clk(CLK), .Q(out_7), .clr(CLR));
  Register #(.trigger("falling"), .width(4)) register_2 (
    .D(in_2[3:0]), .en(n_Li), .clk(CLK), .Q(register_2_q), .clr(CLR));
  assign out_6 = n_Ei ? register_2_q : 4'bz;  // Controlled_Buffer controlled_buffer_1
endmodule

module Controller (
  input  StartClear,
  input  SingleStep,
  input  ManualAuto,
  input  [3:0] in_4,
  output nCLR,
  output CLR,
  output CLK,
  output nCLK,
  output [11:0] out_9
);

  wire clock_1_out, d_ff_2_qn, d_ff_3_q, d_ff_3_qn, j_k_ff_1_q, nand_5_out, nand_6_out, nand_7_out,
       not_1_out, not_2_out, not_3_out, not_4_out, not_5_out, not_6_out, not_7_out, not_8_out, or_1_out,
       undriven, undriven_2, undriven_3;

  not not_1 (not_1_out, in_4[3]);
  not not_2 (not_2_out, in_4[2]);
  not not_3 (not_3_out, in_4[1]);
  not not_4 (not_4_out, in_4[0]);
  // NAND_Gate nand_1 has open pins: in0=not_1_out, in1=not_2_out, in2=not_3_out, in3=not_4_out, out=open
  // NAND_Gate nand_2 has open pins: in0=not_1_out, in1=not_2_out, in2=not_3_out, in3=in_4[0], out=open
  // NAND_Gate nand_3 has open pins: in0=not_1_out, in1=not_2_out, in2=in_4[1], in3=not_4_out, out=open
  // NAND_Gate nand_4 has open pins: in0=in_4[3], in1=in_4[2], in2=in_4[1], in3=not_4_out, out=open
  nand nand_5 (nand_5_out, in_4[3], in_4[2], in_4[1], in_4[0]);
  not not_5 (not_5_out, StartClear);
  not not_6 (not_6_out, SingleStep);
  not not_7 (not_7_out, ManualAuto);
  D_Flip_Flop d_ff_1 (.D(StartClear), .clk(not_5_out), .Q(nCLR), .Qn(CLR));  // open: preset, reset
  D_Flip_Flop d_ff_2 (.D(SingleStep), .clk(not_6_out), .Qn(d_ff_2_qn));  // open: Q, preset, reset
  D_Flip_Flop d_ff_3 (.D(ManualAuto), .clk(not_7_out), .Q(d_ff_3_q), .Qn(d_ff_3_qn));  // open: preset, reset
  Clock clock_1 (.out(clock_1_out));
  J_K_Flip_Flop #(.trigger("falling")) j_k_ff_1 (
    .J(undriven), .K(undriven), .clk(clock_1_out), .Q(j_k_ff_1_q), .reset(undriven_2));  // open: Qn, preset
  nand nand_6 (nand_6_out, undriven_3, d_ff_2_qn, d_ff_3_q);
  nand nand_7 (nand_7_out, d_ff_3_qn, j_k_ff_1_q);
  or or_1 (or_1_out, nand_6_out, nand_7_out);
  not not_8 (not_8_out, or_1_out);
  not not_9 (CLK, not_8_out);
  not not_10 (nCLK, or_1_out);

  // Notes on the sheet:
  //   n_HLT
  //   n_HLT
  //   n_CLR
  //   n_HLT
  //   n_CLR
  //   CLR
endmodule

module AccumulatorA (
  input  [7:0] in_1,
  input  n_La,
  input  CLK,
  input  Ea,
  output [7:0] out_5,
  output [7:0] out_6
);

  Register #(.width(4)) register_1 (.D(in_1[7:4]), .en(n_La), .clk(CLK), .Q(out_6[7:4]));  // open: clr
  assign out_5 = Ea ? out_6 : 8'bz;  // Controlled_Buffer controlled_buffer_1
  Register #(.width(4)) register_2 (.D(in_1[3:0]), .en(n_La), .clk(CLK), .Q(out_6[3:0]));  // open: clr
endmodule

module AdderSubtractor (
  input  [7:0] in_1,
  input  Su,
  input  Eu,
  input  [7:0] in_4,
  output [7:0] out_5
);

  wire xor_1_out, xor_2_out, xor_3_out, xor_4_out, xor_5_out, xor_6_out, xor_7_out, xor_8_out;
  wire [7:0] eightbitadder_1_o8;

  assign out_5 = Eu ? ~eightbitadder_1_o8 : 8'bz;  // Controlled_Inverter controlled_inverter_1
  EightBitAdder eightbitadder_1 (
    .A1(in_1[7]), .A2(in_1[6]), .A3(in_1[5]), .A4(in_1[4]), .A5(in_1[3]), .A6(in_1[2]), .A7(in_1[1]),
    .A8(in_1[0]), .B1(xor_8_out), .B2(xor_7_out), .B3(xor_6_out), .B4(xor_5_out), .B5(xor_4_out),
    .B6(xor_3_out), .B7(xor_2_out), .B8(xor_1_out), .C_in(Su), .O1(eightbitadder_1_o8[7]),
    .O2(eightbitadder_1_o8[6]), .O3(eightbitadder_1_o8[5]), .O4(eightbitadder_1_o8[4]),
    .O5(eightbitadder_1_o8[3]), .O6(eightbitadder_1_o8[2]), .O7(eightbitadder_1_o8[1]),
    .O8(eightbitadder_1_o8[0]));  // open: C_out
  xor xor_1 (xor_1_out, Su, in_4[7]);
  xor xor_2 (xor_2_out, Su, in_4[6]);
  xor xor_3 (xor_3_out, Su, in_4[5]);
  xor xor_4 (xor_4_out, Su, in_4[4]);
  xor xor_5 (xor_5_out, Su, in_4[3]);
  xor xor_6 (xor_6_out, Su, in_4[2]);
  xor xor_7 (xor_7_out, Su, in_4[1]);
  xor xor_8 (xor_8_out, Su, in_4[0]);
endmodule

module BRegister (
  input  n_Lb,
  input  [7:0] in_2,
  input  CLK,
  output [7:0] out_4
);

  Register #(.width(4)) register_1 (.D(in_2[7:4]), .en(n_Lb), .clk(CLK), .Q(out_4[7:4]));  // open: clr
  Register #(.width(4)) register_2 (.D(in_2[3:0]), .en(n_Lb), .clk(CLK), .Q(out_4[3:0]));  // open: clr
endmodule

module OutputRegister (
  input  n_Lo,
  input  [7:0] in_2,
  input  CLK,
  output [7:0] out_4
);

  Register #(.width(4)) register_1 (.D(in_2[7:4]), .en(n_Lo), .clk(CLK), .Q(out_4[7:4]));  // open: clr
  Register #(.width(4)) register_2 (.D(in_2[3:0]), .en(n_Lo), .clk(CLK), .Q(out_4[3:0]));  // open: clr
endmodule

module BinaryDisplay (
  input  [7:0] in_1
);
endmodule

module EightBitAdder (
  input  A1,
  input  A2,
  input  A3,
  input  A4,
  input  A5,
  input  A6,
  input  A7,
  input  A8,
  input  B1,
  input  B2,
  input  B3,
  input  B4,
  input  B5,
  input  B6,
  input  B7,
  input  B8,
  input  C_in,
  output O1,
  output O2,
  output O3,
  output O4,
  output O5,
  output O6,
  output O7,
  output O8,
  output C_out
);

  wire and_1_out, and_2_out, and_3_out, and_4_out, and_5_out, and_6_out, and_7_out, and_8_out, and_9_out,
       and_10_out, and_11_out, and_12_out, and_13_out, and_14_out, and_15_out, and_16_out, xor_1_out,
       xor_3_out, xor_4_out, xor_6_out, xor_7_out, xor_9_out, xor_10_out, xor_12_out, xor_13_out, xor_15_out,
       xor_16_out, xor_18_out, xor_19_out, xor_21_out, xor_22_out;

  and and_1 (and_1_out, A1, B1);
  xor xor_1 (xor_1_out, A1, B1);
  and and_2 (and_2_out, C_in, xor_1_out);
  xor xor_2 (O1, xor_1_out, C_in);
  xor xor_3 (xor_3_out, and_2_out, and_1_out);
  and and_3 (and_3_out, A2, B2);
  xor xor_4 (xor_4_out, A2, B2);
  and and_4 (and_4_out, xor_3_out, xor_4_out);
  xor xor_5 (O2, xor_4_out, xor_3_out);
  xor xor_6 (xor_6_out, and_4_out, and_3_out);
  and and_5 (and_5_out, A3, B3);
  xor xor_7 (xor_7_out, A3, B3);
  and and_6 (and_6_out, xor_6_out, xor_7_out);
  xor xor_8 (O3, xor_7_out, xor_6_out);
  xor xor_9 (xor_9_out, and_6_out, and_5_out);
  and and_7 (and_7_out, A4, B4);
  xor xor_10 (xor_10_out, A4, B4);
  and and_8 (and_8_out, xor_9_out, xor_10_out);
  xor xor_11 (O4, xor_10_out, xor_9_out);
  xor xor_12 (xor_12_out, and_8_out, and_7_out);
  and and_9 (and_9_out, A5, B5);
  xor xor_13 (xor_13_out, A5, B5);
  and and_10 (and_10_out, xor_12_out, xor_13_out);
  xor xor_14 (O5, xor_13_out, xor_12_out);
  xor xor_15 (xor_15_out, and_10_out, and_9_out);
  and and_11 (and_11_out, A6, B6);
  xor xor_16 (xor_16_out, A6, B6);
  and and_12 (and_12_out, xor_15_out, xor_16_out);
  xor xor_17 (O6, xor_16_out, xor_15_out);
  xor xor_18 (xor_18_out, and_12_out, and_11_out);
  and and_13 (and_13_out, A7, B7);
  xor xor_19 (xor_19_out, A7, B7);
  and and_14 (and_14_out, xor_18_out, xor_19_out);
  xor xor_20 (O7, xor_19_out, xor_18_out);
  xor xor_21 (xor_21_out, and_14_out, and_13_out);
  and and_15 (and_15_out, A8, B8);
  xor xor_22 (xor_22_out, A8, B8);
  and and_16 (and_16_out, xor_21_out, xor_22_out);
  xor xor_23 (O8, xor_22_out, xor_21_out);
  xor xor_24 (C_out, and_16_out, and_15_out);
endmodule
